// Logisim project 思考题2格雷码转换.circ as structural Verilog: 1 circuit, main circuit main
module main (
  input  in_1,
  input  in_2,
  input  in_3,
  input  in_4,
  output out_5,
  output out_6,
  output out_7,
  output out_8
);

  xor xor_1 (out_5, in_1, in_2);
  xor xor_2 (out_6, in_2, in_3);
  xor xor_3 (out_7, in_3, in_4);

  assign out_8 = in_4;

  // Other names for the same wires on the sheet: D0 = in_1; D1 = in_2; D2 = in_3; G0 = out_5; G1 = out_6; G2 = out_7;
  //   D3 = in_4; G3 = in_4
endmodule
