// Logisim project 思考题1.circ as structural Verilog: 1 circuit, main circuit main
module main (
  input  in_1,
  input  in_2,
  input  in_3,
  input  in_4,
  input  in_5,
  input  in_6
);

  wire AND1_out, AND2_out, nand_1_out, nand_2_out, not_1_out, not_2_out, Y, Y_prime;

  not not_1 (not_1_out, in_3);
  not not_2 (not_2_out, in_6);
  and AND1 (AND1_out, in_1, not_1_out);
  or OR (Y, AND1_out, AND2_out);
  and AND2 (AND2_out, in_2, in_3);
  nand nand_1 (nand_1_out, in_4, not_2_out);
  nand nand_2 (nand_2_out, in_5, in_6);
  nand nand_3 (Y_prime, nand_1_out, nand_2_out);

  // Other names for the same wires on the sheet: C0 = in_4; C1 = in_5; D0 = in_1; D1 = in_2; S = in_3; S_prime = in_6

  // Notes on the sheet:
  //   与-或电路
  //   与非-与非电路
endmodule
