// Logisim project 思考题3奇偶校验.circ as structural Verilog: 1 circuit, main circuit main
module main (
  input  in_1,
  input  in_2,
  input  in_3,
  input  in_4,
  output out_5,
  output out_6
);

  wire xor_1_out, xor_2_out;

  xor xor_1 (xor_1_out, in_1, in_2);
  xor xor_2 (xor_2_out, xor_1_out, in_3);
  xor xor_3 (out_6, xor_2_out, in_4);
  not not_1 (out_5, out_6);

  // Other names for the same wires on the sheet: EVEN = out_5; N0 = in_1; N1 = in_2; N2 = in_3; N3 = in_4;
  //   ODD = out_6
endmodule
