// Logisim project 思考题1.circ as structural Verilog: 2 circuits, main circuit main
module main (
  input  [3:0] X,
  input  [3:0] Y,
  input  Cin,
  output [3:0] F,
  output Cout
);

  wire CF, FA0_cout, FA1_cout, FA2_cout, OF, xor_1_out, xor_2_out, xor_3_out, xor_4_out, ZF;

  Hex_Digit_Display hex_digit_display_1 (.value(X));  // open: dp
  Hex_Digit_Display hex_digit_display_2 (.value(Y));  // open: dp
  FA FA0 (.A(X[0]), .B(xor_1_out), .Cin(Cin), .Cout(FA0_cout), .F(F[0]));
  xor xor_1 (xor_1_out, Cin, Y[0]);
  Hex_Digit_Display hex_digit_display_3 (.value(F));  // open: dp
  FA FA1 (.A(X[1]), .B(xor_2_out), .Cin(FA0_cout), .Cout(FA1_cout), .F(F[1]));
  xor xor_2 (xor_2_out, Cin, Y[1]);
  FA FA2 (.A(X[2]), .B(xor_3_out), .Cin(FA1_cout), .Cout(FA2_cout), .F(F[2]));
  xor xor_3 (xor_3_out, Cin, Y[2]);
  xor xor_4 (xor_4_out, Cin, Y[3]);
  nor nor_1 (ZF, F[0], F[1], F[2], F[3]);
  FA FA3 (.A(X[3]), .B(xor_4_out), .Cin(FA2_cout), .Cout(Cout), .F(F[3]));
  xor xor_5 (CF, Cout, Cin);
  xor xor_6 (OF, Cout, FA2_cout);

  // Other names for the same wires on the sheet: SUM[3:0] = F; SF = F[3]; 操作数x[3:0] = X; 操作数y[3:0] = Y

  // Notes on the sheet:
  //   输入引脚
  //   +
  //   =
  //   请勿修改引脚名称、电路名称及电路封装外观
  //   提示：使用独立逻辑门及全加器FA子电路实现4位二进制数加减法器，禁止直接使用加减法器组件。
  //   输出引脚
endmodule

module FA (
  input  A,
  input  B,
  input  Cin,
  output F,
  output Cout
);

  wire nand_1_out, nand_2_out, nand_3_out, xor_1_out;

  nand nand_1 (nand_1_out, A, B);
  nand nand_2 (nand_2_out, B, Cin);
  nand nand_3 (nand_3_out, A, Cin);
  xor xor_1 (xor_1_out, A, B);
  xor xor_2 (F, xor_1_out, Cin);
  nand nand_4 (Cout, nand_1_out, nand_2_out, nand_3_out);

  // Notes on the sheet:
  //   全加器
endmodule
