// Logisim project 思考题3.circ as structural Verilog: 1 circuit, main circuit main
module main (
  input  [3:0] in_1,
  input  [3:0] in_2,
  output out_3,
  output out_4,
  output out_5
);

  wire and_1_out, and_2_out, and_3_out, and_4_out, and_5_out, and_6_out, and_7_out, and_8_out, and_9_out,
       and_10_out, xnor_1_out, xnor_2_out, xnor_3_out, xnor_4_out;

  and and_1 (and_1_out, in_1[3], ~in_2[3]);  // AND_Gate
  xnor xnor_1 (xnor_1_out, in_1[3], in_2[3]);
  and and_2 (and_2_out, ~in_1[3], in_2[3]);  // AND_Gate
  and and_3 (and_3_out, in_1[2], ~in_2[2], xnor_1_out);  // AND_Gate
  xnor xnor_2 (xnor_2_out, in_1[2], in_2[2]);
  and and_4 (and_4_out, xnor_2_out, xnor_1_out);
  and and_5 (and_5_out, ~in_1[2], in_2[2], xnor_1_out);  // AND_Gate
  and and_6 (and_6_out, in_1[1], ~in_2[1], and_4_out);  // AND_Gate
  xnor xnor_3 (xnor_3_out, in_1[1], in_2[1]);
  and and_7 (and_7_out, ~in_1[1], in_2[1], and_4_out);  // AND_Gate
  and and_8 (and_8_out, xnor_3_out, and_4_out);
  and and_9 (and_9_out, in_1[0], ~in_2[0], and_8_out);  // AND_Gate
  xnor xnor_4 (xnor_4_out, in_1[0], in_2[0]);
  and and_10 (and_10_out, ~in_1[0], in_2[0], and_8_out);  // AND_Gate
  or or_1 (out_3, and_9_out, and_6_out, and_3_out, and_1_out);
  and and_11 (out_4, xnor_4_out, and_8_out);
  or or_2 (out_5, and_2_out, and_5_out, and_7_out, and_10_out);

  // Other names for the same wires on the sheet: X[3:0] = in_1; X__Y = out_4; X_Y = out_5; X_Y_t = out_3;
  //   Y[3:0] = in_2
endmodule
