// Logisim project 思考题4.circ as structural Verilog: 3 circuits, main circuit main
module main (
  input  [31:0] in_1,
  input  in_2,
  input  [4:0] in_3,
  input  in_4,
  output [31:0] Dout,
  output [31:0] out_6
);

  wire [7:0] barrelsft8b_1_dataout, \barrelsft8b改_1_dataout , \barrelsft8b改_2_dataout ,
       \barrelsft8b改_3_dataout , \barrelsft8b改_4_dataout , \barrelsft8b改_5_dataout ,
       \barrelsft8b改_6_dataout , \barrelsft8b改_7_dataout , multiplexer_4_out;
  wire [15:0] multiplexer_2_out;
  wire [31:0] multiplexer_3_out;
  wire [31:31] multiplexer_1_out;

  Multiplexer #(.enable("false")) multiplexer_1 (.in0(1'b0), .in1(in_1[31]), .out(multiplexer_1_out[31]), .sel(in_2));
  Multiplexer #(.width(16), .enable("false")) multiplexer_2 (
    .in0({16{1'b0}}), .in1(in_1[31:16]), .out(multiplexer_2_out), .sel(in_2));
  Multiplexer #(.select(2), .width(32), .enable("false")) multiplexer_3 (
    .in0(in_1), .in1({{16{multiplexer_1_out[31]}}, in_1[31:16]}), .in2(in_1),
    .in3({in_1[15:0], multiplexer_2_out}), .out(multiplexer_3_out), .sel({in_4, in_3[4]}));
  Multiplexer #(.width(8), .enable("false")) multiplexer_4 (
    .in0({8{1'b0}}), .in1(multiplexer_3_out[31:24]), .out(multiplexer_4_out), .sel(in_2));
  Multiplexer #(.select(2), .width(32), .enable("false")) multiplexer_5 (
    .in0(multiplexer_3_out), .in1({{8{multiplexer_1_out[31]}}, multiplexer_3_out[31:8]}),
    .in2(multiplexer_3_out), .in3({multiplexer_3_out[23:0], multiplexer_4_out}), .out(out_6),
    .sel({in_4, in_3[3]}));
  \BarrelSFT8b改  \barrelsft8b改_1  (
    .DataIn(out_6[7:0]), .shamt(in_3[2:0]), .DataOut(\barrelsft8b改_1_dataout ), .L_R(1'b1), .A_L(in_2),
    .\input (out_6[31:24]));
  \BarrelSFT8b改  \barrelsft8b改_2  (
    .DataIn(out_6[15:8]), .shamt(in_3[2:0]), .DataOut(\barrelsft8b改_2_dataout ), .L_R(1'b1), .A_L(1'b1),
    .\input (out_6[7:0]));
  \BarrelSFT8b改  \barrelsft8b改_3  (
    .DataIn(out_6[23:16]), .shamt(in_3[2:0]), .DataOut(\barrelsft8b改_3_dataout ), .L_R(1'b1), .A_L(1'b1),
    .\input (out_6[15:8]));
  \BarrelSFT8b改  \barrelsft8b改_4  (
    .DataIn(out_6[31:24]), .shamt(in_3[2:0]), .DataOut(\barrelsft8b改_4_dataout ), .L_R(1'b1), .A_L(1'b1),
    .\input (out_6[23:16]));
  \BarrelSFT8b改  \barrelsft8b改_5  (
    .DataIn(out_6[7:0]), .shamt(in_3[2:0]), .DataOut(\barrelsft8b改_5_dataout ), .L_R(1'b0), .A_L(1'b1),
    .\input (out_6[15:8]));
  \BarrelSFT8b改  \barrelsft8b改_6  (
    .DataIn(out_6[15:8]), .shamt(in_3[2:0]), .DataOut(\barrelsft8b改_6_dataout ), .L_R(1'b0), .A_L(1'b1),
    .\input (out_6[23:16]));
  \BarrelSFT8b改  \barrelsft8b改_7  (
    .DataIn(out_6[23:16]), .shamt(in_3[2:0]), .DataOut(\barrelsft8b改_7_dataout ), .L_R(1'b0), .A_L(1'b1),
    .\input (out_6[31:24]));
  BarrelSFT8b barrelsft8b_1 (
    .DataIn(out_6[31:24]), .shamt(in_3[2:0]), .DataOut(barrelsft8b_1_dataout), .L_R(1'b0), .A_L(in_2));
  Multiplexer #(.width(32), .enable("false")) multiplexer_6 (
    .in0({barrelsft8b_1_dataout, \barrelsft8b改_7_dataout , \barrelsft8b改_6_dataout , \barrelsft8b改_5_dataout }),
    .in1({\barrelsft8b改_4_dataout , \barrelsft8b改_3_dataout , \barrelsft8b改_2_dataout , \barrelsft8b改_1_dataout }),
    .out(Dout), .sel(in_4));

  // Other names for the same wires on the sheet: Din[31:0] = in_1; shampt[4:0] = in_3; L_R = in_4; A_L = in_2

  // Notes on the sheet:
  //   AL  LR: 00右移0，10右移符号位，01左移0，11循环左移
endmodule

module \BarrelSFT8b改  (
  input  [7:0] DataIn,
  input  [2:0] shamt,
  input  [7:0] \input ,
  input  L_R,
  input  A_L,
  output [7:0] DataOut
);

  wire [0:0] multiplexer_1_out;
  wire [1:0] multiplexer_4_out, multiplexer_5_out;
  wire [3:0] multiplexer_7_out, multiplexer_8_out;
  wire [7:0] input1, input2, input3, multiplexer_3_out, multiplexer_6_out;
  wire [7:7] multiplexer_2_out;

  Multiplexer #(.enable("false")) multiplexer_1 (.in0(1'b0), .in1(\input [7]), .out(multiplexer_1_out[0]), .sel(A_L));
  Multiplexer #(.enable("false")) multiplexer_2 (.in0(1'b0), .in1(\input [0]), .out(multiplexer_2_out[7]), .sel(A_L));
  BarrelSFT8b barrelsft8b_1 (.DataIn(\input ), .shamt({2'b00, shamt[0]}), .DataOut(input1), .L_R(L_R), .A_L(A_L));
  Multiplexer #(.select(2), .width(8), .enable("false")) multiplexer_3 (
    .in0(DataIn), .in1({multiplexer_2_out[7], DataIn[7:1]}), .in2(DataIn),
    .in3({DataIn[6:0], multiplexer_1_out[0]}), .out(multiplexer_3_out), .sel({L_R, shamt[0]}));
  Multiplexer #(.width(2), .enable("false")) multiplexer_4 (
    .in0(2'b00), .in1(input1[1:0]), .out(multiplexer_4_out), .sel(A_L));
  Multiplexer #(.width(2), .enable("false")) multiplexer_5 (
    .in0(2'b00), .in1(input1[7:6]), .out(multiplexer_5_out), .sel(A_L));
  Multiplexer #(.select(2), .width(8), .enable("false")) multiplexer_6 (
    .in0(multiplexer_3_out), .in1({multiplexer_4_out, multiplexer_3_out[7:2]}), .in2(multiplexer_3_out),
    .in3({multiplexer_3_out[5:0], multiplexer_5_out}), .out(multiplexer_6_out), .sel({L_R, shamt[1]}));
  BarrelSFT8b barrelsft8b_2 (.DataIn(input1), .shamt({1'b0, shamt[1], 1'b0}), .DataOut(input2), .L_R(L_R), .A_L(A_L));
  Multiplexer #(.width(4), .enable("false")) multiplexer_7 (
    .in0(4'b0000), .in1(input2[3:0]), .out(multiplexer_7_out), .sel(A_L));
  Multiplexer #(.width(4), .enable("false")) multiplexer_8 (
    .in0(4'b0000), .in1(input2[7:4]), .out(multiplexer_8_out), .sel(A_L));
  Multiplexer #(.select(2), .width(8), .enable("false")) multiplexer_9 (
    .in0(multiplexer_6_out), .in1({multiplexer_7_out, multiplexer_6_out[7:4]}), .in2(multiplexer_6_out),
    .in3({multiplexer_6_out[3:0], multiplexer_8_out}), .out(DataOut), .sel({L_R, shamt[2]}));
  BarrelSFT8b barrelsft8b_3 (.DataIn(input2), .shamt({shamt[2], 2'b00}), .DataOut(input3), .L_R(L_R), .A_L(A_L));

  // Other names for the same wires on the sheet: Din[7:0] = DataIn; Left_Right = L_R; Arth_Logic = A_L;
  //   Dout[7:0] = DataOut

  // Notes on the sheet:
  //   L/R,A/L: 00逻辑右移，01算术右移，10逻辑左移，11：循环左移
  //   输入引脚
  //   请勿修改引脚名称、电路名称及电路封装外观
  //   提示：使用多路选择器级联实现8位桶形移位器，禁止直接使用移位器组件。
  //   输出引脚
endmodule

module BarrelSFT8b (
  input  [7:0] DataIn,
  input  [2:0] shamt,
  input  L_R,
  input  A_L,
  output [7:0] DataOut
);

  wire [0:0] multiplexer_1_out;
  wire [1:0] multiplexer_4_out;
  wire [3:0] multiplexer_6_out;
  wire [7:0] multiplexer_3_out, multiplexer_5_out;
  wire [7:7] multiplexer_2_out;

  Multiplexer #(.enable("false")) multiplexer_1 (.in0(1'b0), .in1(DataIn[7]), .out(multiplexer_1_out[0]), .sel(A_L));
  Multiplexer #(.enable("false")) multiplexer_2 (.in0(1'b0), .in1(DataIn[7]), .out(multiplexer_2_out[7]), .sel(A_L));
  Multiplexer #(.select(2), .width(8), .enable("false")) multiplexer_3 (
    .in0(DataIn), .in1({multiplexer_2_out[7], DataIn[7:1]}), .in2(DataIn),
    .in3({DataIn[6:0], multiplexer_1_out[0]}), .out(multiplexer_3_out), .sel({L_R, shamt[0]}));
  Multiplexer #(.width(2), .enable("false")) multiplexer_4 (
    .in0(2'b00), .in1(multiplexer_3_out[7:6]), .out(multiplexer_4_out), .sel(A_L));
  Multiplexer #(.select(2), .width(8), .enable("false")) multiplexer_5 (
    .in0(multiplexer_3_out), .in1({{2{multiplexer_2_out[7]}}, multiplexer_3_out[7:2]}),
    .in2(multiplexer_3_out), .in3({multiplexer_3_out[5:0], multiplexer_4_out}), .out(multiplexer_5_out),
    .sel({L_R, shamt[1]}));
  Multiplexer #(.width(4), .enable("false")) multiplexer_6 (
    .in0(4'b0000), .in1(multiplexer_5_out[7:4]), .out(multiplexer_6_out), .sel(A_L));
  Multiplexer #(.select(2), .width(8), .enable("false")) multiplexer_7 (
    .in0(multiplexer_5_out), .in1({{4{multiplexer_2_out[7]}}, multiplexer_5_out[7:4]}),
    .in2(multiplexer_5_out), .in3({multiplexer_5_out[3:0], multiplexer_6_out}), .out(DataOut),
    .sel({L_R, shamt[2]}));

  // Other names for the same wires on the sheet: Din[7:0] = DataIn; Left_Right = L_R; Arth_Logic = A_L;
  //   Dout[7:0] = DataOut

  // Notes on the sheet:
  //   L/R,A/L: 00逻辑右移，01算术右移，10逻辑左移，11：循环左移
  //   输入引脚
  //   请勿修改引脚名称、电路名称及电路封装外观
  //   提示：使用多路选择器级联实现8位桶形移位器，禁止直接使用移位器组件。
  //   输出引脚
endmodule
