// Logisim project thinking1.circ as structural Verilog: 1 circuit, main circuit main
module main (
  input  [31:0] X1,
  input  [31:0] X0,
  input  [31:0] Y1,
  input  [31:0] Y0,
  input  Cin,
  output out_6,
  output [31:0] Z1,
  output out_8,
  output out_9,
  output [31:0] Z0
);

  wire clu4_1_c1, clu4_1_c2, clu4_1_c3, main_1_gg, main_1_pg, main_2_gg, main_2_pg, main_3_gg, main_3_pg,
       main_4_pg;

  lab4_2_main main_1 (
    .X(X1[31:16]), .Y(Y1[31:16]), .C0(clu4_1_c3), .S(Z1[31:16]), .C16(out_9), .Pg(main_1_pg), .Gg(main_1_gg));
  lab4_2_main main_2 (
    .X(X1[15:0]), .Y(Y1[15:0]), .C0(clu4_1_c2), .S(Z1[15:0]), .Pg(main_2_pg), .Gg(main_2_gg));  // open: C16
  CLU4 clu4_1 (
    .P0(main_4_pg), .P1(main_3_pg), .P2(main_2_pg), .P3(main_1_pg), .C1(clu4_1_c1), .C3(clu4_1_c3),
    .G0(main_4_pg), .G1(main_3_gg), .G2(main_2_gg), .G3(main_1_gg), .C2(clu4_1_c2), .C0(Cin), .Pg(out_6),
    .Gg(out_8));  // open: C4
  lab4_2_main main_3 (
    .X(X0[31:16]), .Y(Y0[31:16]), .C0(clu4_1_c1), .S(Z0[31:16]), .Pg(main_3_pg), .Gg(main_3_gg));  // open: C16
  lab4_2_main main_4 (.X(X0[15:0]), .Y(Y0[15:0]), .C0(Cin), .S(Z0[15:0]), .Pg(main_4_pg), .Gg(main_4_pg));  // open: C16

  // Other names for the same wires on the sheet: C64 = out_9; Gg = out_8; Pg = out_6
endmodule
