// Logisim project thinking2.circ as structural Verilog: 3 circuits, main circuit main
module main (
  input  in_1,
  input  in_2,
  input  [31:0] in_3,
  input  [31:0] in_4,
  output [31:0] out_5,
  output [31:0] out_6
);

  wire and_1_out, LOAD, not_1_out, STOP;
  wire [0:0] adder32_1_s_2;
  wire [5:0] counter_1_q;
  wire [31:0] adder32_1_s, multiplexer_1_out, multiplexer_2_out;

  not not_1 (not_1_out, STOP);
  Multiplexer #(.width(32), .enable("false")) multiplexer_1 (
    .in0({32{1'b0}}), .in1(in_3), .out(multiplexer_1_out), .sel(out_6[0]));
  Register #(.width(32), .Select("low")) register_1 (
    .D(adder32_1_s), .en(not_1_out), .Q(out_5), .clk(in_1), .clr(in_2));
  Adder32 adder32_1 (
    .Cin(1'b0), .Cout(adder32_1_s[31]), .X(multiplexer_1_out), .Y(out_5),
    .S({adder32_1_s[30:0], adder32_1_s_2[0]}));  // open: OF, CF, ZF, SF
  Register #(.width(32), .Select("low")) register_2 (
    .D(multiplexer_2_out), .en(not_1_out), .Q(out_6), .clk(in_1), .clr(in_2));
  Multiplexer #(.width(32), .enable("false")) multiplexer_2 (
    .in0({adder32_1_s_2[0], out_6[31:1]}), .in1(in_4), .out(multiplexer_2_out), .sel(LOAD));
  and and_1 (and_1_out, in_1, not_1_out);
  Counter #(.width(6), .max('h3f)) counter_1 (
    .D({6{1'b0}}), .Q(counter_1_q), .clk(and_1_out), .clr(in_2));  // open: load, count, carry, preset, down
  Comparator #(.width(6), .mode("unsigned")) comparator_1 (.a(counter_1_q), .b({6{1'b0}}), .eq(LOAD));  // open: gt, lt
  Comparator #(.width(6), .mode("unsigned")) comparator_2 (.a(counter_1_q), .b(6'b100001), .eq(STOP));  // open: gt, lt

  // Other names for the same wires on the sheet: Z0[31:0] = out_6; CLK = in_1; RST = in_2; X[31:0] = in_3;
  //   Y[31:0] = in_4; Z1[31:0] = out_5
endmodule

module ALUctrl (
  input  [3:0] ALUctr,
  output SUBctr,
  output LRctr,
  output SIGctr,
  output ALctr,
  output [2:0] OPctr
);

  wire and_2_out, and_3_out, and_6_out, and_7_out, and_8_out, and_9_out, and_10_out, and_11_out, and_12_out,
       and_13_out, and_14_out, and_15_out, and_16_out;

  and and_1 (SIGctr, ~ALUctr[0], ALUctr[1], ~ALUctr[2], ~ALUctr[3]);  // AND_Gate
  and and_2 (and_2_out, ALUctr[1], ~ALUctr[2], ~ALUctr[3]);  // AND_Gate
  and and_3 (and_3_out, ~ALUctr[0], ~ALUctr[1], ~ALUctr[2], ALUctr[3]);  // AND_Gate
  and and_4 (ALctr, ALUctr[0], ~ALUctr[1], ALUctr[2], ALUctr[3]);  // AND_Gate
  and and_5 (LRctr, ALUctr[0], ~ALUctr[1], ~ALUctr[2], ~ALUctr[3]);  // AND_Gate
  and and_6 (and_6_out, ALUctr[0], ALUctr[2], ALUctr[3]);
  and and_7 (and_7_out, ALUctr[0], ~ALUctr[1], ALUctr[2]);  // AND_Gate
  and and_8 (and_8_out, ALUctr[0], ~ALUctr[1], ~ALUctr[3]);  // AND_Gate
  and and_9 (and_9_out, ALUctr[0], ~ALUctr[2], ~ALUctr[3]);  // AND_Gate
  and and_10 (and_10_out, ALUctr[0], ~ALUctr[1], ~ALUctr[2], ALUctr[3]);  // AND_Gate
  and and_11 (and_11_out, ALUctr[1], ~ALUctr[2], ~ALUctr[3]);  // AND_Gate
  and and_12 (and_12_out, ~ALUctr[3], ALUctr[2], ~ALUctr[0]);  // AND_Gate
  and and_13 (and_13_out, ~ALUctr[0], ALUctr[1], ~ALUctr[3]);  // AND_Gate
  and and_14 (and_14_out, ~ALUctr[0], ~ALUctr[1], ALUctr[2], ~ALUctr[3]);  // AND_Gate
  and and_15 (and_15_out, ALUctr[0], ALUctr[1], ALUctr[2], ~ALUctr[3]);  // AND_Gate
  and and_16 (and_16_out, ALUctr[0], ALUctr[1], ALUctr[2], ALUctr[3]);
  or or_1 (SUBctr, and_2_out, and_3_out);
  or or_2 (OPctr[1], and_10_out, and_12_out, and_11_out, and_13_out);
  or or_3 (OPctr[2], and_6_out, and_8_out, and_7_out, and_9_out, and_10_out, and_11_out);
  or or_4 (OPctr[0], and_14_out, and_15_out, and_16_out, and_10_out);

  // Notes on the sheet:
  //   输入引脚
  //   ALU操作控制信号生成部件
  //   输出引脚
endmodule

module ALU (
  input  [3:0] ALUctr,
  input  [31:0] A,
  input  [31:0] B,
  output Zero,
  output [31:0] S
);

  wire adder32_1_cf, adder32_1_of, adder32_1_sf, aluctrl_1_alctr, aluctrl_1_lrctr, aluctrl_1_sigctr,
       aluctrl_1_subctr, multiplexer_2_out, xor_3_out;
  wire [2:0] aluctrl_1_opctr;
  wire [31:0] adder32_1_s, and_1_out, bit_extender_1_out, bit_extender_2_out, main_1_dataout,
       multiplier_1_out, or_1_out, xor_1_out, xor_2_out;

  assign xor_1_out = B ^ bit_extender_1_out;  // XOR_Gate xor_1, 32 bits wide
  assign bit_extender_1_out = {{31{aluctrl_1_subctr}}, aluctrl_1_subctr};  // Bit_Extender bit_extender_1
  assign and_1_out = A & B;  // AND_Gate and_1, 32 bits wide
  assign or_1_out = A | B;  // OR_Gate or_1, 32 bits wide
  assign xor_2_out = A ^ B;  // XOR_Gate xor_2, 32 bits wide
  lab4_4_main main_1 (
    .L_R(aluctrl_1_lrctr), .shamt(B[4:0]), .DataIn(A), .DataOut(main_1_dataout), .A_L(aluctrl_1_alctr));
  Multiplier #(.width(32)) multiplier_1 (.a(A), .b(B), .out(multiplier_1_out));  // open: cin, cout
  Adder32 adder32_1 (
    .Cin(aluctrl_1_subctr), .X(A), .Y(xor_1_out), .S(adder32_1_s), .OF(adder32_1_of), .CF(adder32_1_cf),
    .ZF(Zero), .SF(adder32_1_sf));  // open: Cout
  xor xor_3 (xor_3_out, adder32_1_of, adder32_1_sf);
  Multiplexer #(.select(3), .width(32), .enable("false")) multiplexer_1 (
    .in0(adder32_1_s), .in1(and_1_out), .in2(or_1_out), .in3(xor_2_out), .in4(main_1_dataout), .in5(B),
    .in6(bit_extender_2_out), .in7(multiplier_1_out), .out(S), .sel(aluctrl_1_opctr));
  ALUctrl aluctrl_1 (
    .SUBctr(aluctrl_1_subctr), .LRctr(aluctrl_1_lrctr), .SIGctr(aluctrl_1_sigctr), .ALctr(aluctrl_1_alctr),
    .OPctr(aluctrl_1_opctr), .ALUctr(ALUctr));
  Multiplexer #(.enable("false")) multiplexer_2 (
    .in0(adder32_1_cf), .in1(xor_3_out), .out(multiplexer_2_out), .sel(aluctrl_1_sigctr));
  // Probe on A
  // Probe on B
  // Probe on S
  assign bit_extender_2_out = {{31{1'b0}}, multiplexer_2_out};  // Bit_Extender bit_extender_2

  // Other names for the same wires on the sheet: Result[31:0] = S

  // Notes on the sheet:
  //   B: pull=down
  //   A: pull=down
  //   ALUctr: pull=down
  //   输入引脚
  //   请勿修改引脚名称、电路名称及电路封装外观
  //   提示：使用32位并行加法器子电路、桶形移位器、ALU控制子电路实现32位ALU
  //   功能说明:32位ALU，输入32位操作数A、B，4位控制信号ALUctr，输出32位结果Reseult和1位Zero标志位
  //   输出引脚
  //   操作数和结果
endmodule
